// Digital circuit MMP-1.dig as structural Verilog
module MMP_1 (
  input  clk
);

  wire Addr_Dest, Addr_Src, Addr_Step, alu_1_data_ready, and_1_out, and_2_out, and_3_out, and_4_out,
       and_5_out, and_6_out, and_7_out, and_8_out, and_9_out, and_10_out, and_11_out, and_12_out, and_13_out,
       and_14_out, Clk_out, Clk_t, comparator_1_eq, comparator_2_eq, comparator_2_gt, comparator_2_lt,
       comparator_3_lt, comparator_4_eq, comparator_5_eq, comparator_6_eq, comparator_7_eq, counter_1_ovf,
       dipswitch_1_out, nClk, not_1_out, nRst, or_1_out, Out_Dev, Res_out, Rst, Step_Inc;
  wire [1:0] counter_1_out, counter_2_out;
  wire [4:0] DispXIndex_q;
  wire [10:0] Addr_Match_out;
  wire [15:0] Addr, Dest, multiplexer_2_out, multiplexer_3_out, multiplexer_12_out, multiplexer_12_out_2,
       PrgmStep, Src;
  wire [31:0] alu_1_data_out, DispA, DispB, DispCValues_q, multiplexer_1_out, multiplexer_5_out,
       multiplexer_6_out, multiplexer_7_out, multiplexer_9_out, multiplexer_10_out, multiplexer_11_out,
       ramdualport_1_d, rom_1_d, Temp_q;

  Button Res (.out(Res_out));
  RS_FF_AS rs_ff_as_1 (.S(Res_out), .R(counter_1_ovf), .Q(Rst), .nQ(nRst));
  Register #(.Bits(32)) Temp (.D({multiplexer_12_out_2, multiplexer_12_out}), .C(Clk_t), .en(Addr_Src), .Q(Temp_q));
  Register #(.Bits(16)) u_Src (.D(multiplexer_12_out_2), .C(Clk_t), .en(Addr_Step), .Q(Src));
  Register #(.Bits(16)) u_Dest (.D(multiplexer_12_out), .C(Clk_t), .en(Addr_Step), .Q(Dest));
  Comparator #(.Bits(16)) comparator_1 (.a(Dest), .b({16{1'b1}}), .eq(comparator_1_eq));  // open: gt, lt
  and and_1 (and_1_out, Addr_Dest, comparator_1_eq);
  CounterPreset #(.Bits(16)) Step (
    .en(and_2_out), .C(Clk_t), .dir(1'b0), .in(multiplexer_12_out), .ld(and_1_out), .clr(Rst), .out(PrgmStep));  // open: ovf
  Multiplexer #(.Bits(32)) multiplexer_1 (.sel(Addr_Dest), .in_0({32{1'b0}}), .in_1(Temp_q), .out(multiplexer_1_out));
  and and_2 (and_2_out, Step_Inc, not_1_out);
  Counter #(.Bits(2)) counter_1 (.en(Rst), .C(nClk), .clr(1'b0), .out(counter_1_out), .ovf(counter_1_ovf));
  Multiplexer #(.Bits(16)) multiplexer_2 (.sel(Addr_Src), .in_0({16{1'b0}}), .in_1(Src), .out(multiplexer_2_out));
  Multiplexer #(.Bits(16)) multiplexer_3 (
    .sel(Addr_Dest), .in_0(multiplexer_2_out), .in_1(Dest), .out(multiplexer_3_out));
  not not_1 (not_1_out, comparator_1_eq);
  Multiplexer #(.Bits(16)) multiplexer_4 (.sel(Addr_Step), .in_0(multiplexer_3_out), .in_1(PrgmStep), .out(Addr));
  Comparator #(.Bits(16)) comparator_2 (
    .a(Addr), .b(16'h4000), .gt(comparator_2_gt), .eq(comparator_2_eq), .lt(comparator_2_lt));
  Comparator #(.Bits(16)) comparator_3 (.a(Addr), .b(16'h8000), .lt(comparator_3_lt));  // open: gt, eq
  LookUpTable #(.Bits(11)) Addr_Match (
    .in0(Addr[0]), .in1(Addr[1]), .in2(Addr[2]), .in3(Addr[3]), .in4(Addr[4]), .in5(Addr[5]), .in6(Addr[6]),
    .in7(Addr[7]), .in8(Addr[8]), .in9(Addr[9]), .in10(Addr[10]), .in11(Addr[11]), .in12(Addr[12]),
    .in13(Addr[13]), .in14(Addr[14]), .in15(Addr[15]), .out(Addr_Match_out));
  // Probe Source on Src
  // Probe Destination on Dest
  or or_1 (or_1_out, comparator_2_gt, comparator_2_eq);
  and and_3 (and_3_out, or_1_out, comparator_3_lt);
  // Probe Program Step on PrgmStep
  // Probe Address on Addr
  // Probe Bus on {multiplexer_12_out_2, multiplexer_12_out}
  and and_4 (and_4_out, comparator_2_lt, Out_Dev);
  and and_5 (and_5_out, Addr_Dest, and_3_out);
  and and_6 (and_6_out, and_3_out, Out_Dev);
  ALU alu_1 (
    .Ctrl_In(Addr_Dest), .Ctrl_Out(Out_Dev), .Clk(Clk_t),
    .Data_In({multiplexer_12_out_2, multiplexer_12_out}), .Sel_A(Addr_Match_out[0]),
    .Sel_B(Addr_Match_out[1]), .Sel_SUM(Addr_Match_out[2]), .Sel_AND(Addr_Match_out[3]),
    .Sel_OR(Addr_Match_out[4]), .Sel_XOR(Addr_Match_out[5]), .Sel_NOT(Addr_Match_out[6]),
    .Sel_GT(Addr_Match_out[7]), .Sel_GTE(Addr_Match_out[8]), .Sel_LT(Addr_Match_out[9]),
    .Sel_LTE(Addr_Match_out[10]), .Data_Out(alu_1_data_out), .Data_Ready(alu_1_data_ready));
  ROM #(.bigEndian("true"), .AddrBits(14), .Bits(32)) rom_1 (.A(Addr[13:0]), .sel(1'b1), .D(rom_1_d));
  RAMDualPort #(.AddrBits(14), .Bits(32)) ramdualport_1 (
    .A(Addr[13:0]), .Din({multiplexer_12_out_2, multiplexer_12_out}), .str(and_5_out), .C(Clk_t), .ld(1'b1),
    .D(ramdualport_1_d));
  Counter #(.Bits(2)) counter_2 (.en(1'b1), .C(nClk), .clr(Rst), .out(counter_2_out));  // open: ovf
  // Probe Copy Step on counter_2_out
  Decoder #(.Selector_Bits(2)) decoder_1 (
    .sel(counter_2_out), .out_0(Addr_Step), .out_1(Addr_Src), .out_2(Addr_Dest), .out_3(Step_Inc));
  Multiplexer #(.Bits(32)) multiplexer_5 (
    .sel(and_4_out), .in_0(multiplexer_1_out), .in_1(rom_1_d), .out(multiplexer_5_out));
  Multiplexer #(.Bits(32)) multiplexer_6 (
    .sel(and_6_out), .in_0(multiplexer_5_out), .in_1(ramdualport_1_d), .out(multiplexer_6_out));
  Multiplexer #(.Bits(32)) multiplexer_7 (
    .sel(alu_1_data_ready), .in_0(multiplexer_6_out), .in_1(alu_1_data_out), .out(multiplexer_7_out));
  or or_2 (Out_Dev, Addr_Src, Addr_Step);
  Comparator #(.Bits(16)) comparator_4 (.a(Addr), .b(16'hf100), .eq(comparator_4_eq));  // open: gt, lt
  Comparator #(.Bits(16)) comparator_5 (.a(Addr), .b(16'hf101), .eq(comparator_5_eq));  // open: gt, lt
  Comparator #(.Bits(16)) comparator_6 (.a(Addr), .b(16'hf200), .eq(comparator_6_eq));  // open: gt, lt
  Comparator #(.Bits(16)) comparator_7 (.a(Addr), .b(16'hf201), .eq(comparator_7_eq));  // open: gt, lt
  and and_7 (and_7_out, Addr_Dest, comparator_4_eq);
  and and_8 (and_8_out, comparator_4_eq, Out_Dev);
  and and_9 (and_9_out, Addr_Dest, comparator_5_eq);
  and and_10 (and_10_out, comparator_5_eq, Out_Dev);
  and and_11 (and_11_out, Addr_Dest, comparator_6_eq);
  and and_12 (and_12_out, comparator_6_eq, Out_Dev);
  and and_13 (and_13_out, Addr_Dest, comparator_7_eq);
  and and_14 (and_14_out, comparator_7_eq, Out_Dev);
  LED led_1 (.in(Addr_Step));
  LED led_2 (.in(Addr_Src));
  LED led_3 (.in(Addr_Dest));
  LED led_4 (.in(Step_Inc));
  Register #(.Bits(32)) u_DispA (.D({multiplexer_12_out_2, multiplexer_12_out}), .C(Clk_t), .en(and_7_out), .Q(DispA));
  Register #(.Bits(32)) u_DispB (.D({multiplexer_12_out_2, multiplexer_12_out}), .C(Clk_t), .en(and_9_out), .Q(DispB));
  Register #(.Bits(5)) DispXIndex (.D(multiplexer_12_out[4:0]), .C(Clk_t), .en(and_11_out), .Q(DispXIndex_q));
  Register #(.Bits(32)) DispCValues (
    .D({multiplexer_12_out_2, multiplexer_12_out}), .C(Clk_t), .en(and_13_out), .Q(DispCValues_q));
  Button u_Clk (.out(Clk_out));
  LedMatrix #(.colAddrBits(5), .rowDataBits(32)) ledmatrix_1 (.rows(DispCValues_q), .column(DispXIndex_q));
  Multiplexer multiplexer_8 (.sel(dipswitch_1_out), .in_0(Clk_out), .in_1(clk), .out(Clk_t));
  DipSwitch dipswitch_1 (.out(dipswitch_1_out));
  not not_2 (nClk, Clk_t);
  // Probe Clk on Clk_t
  Multiplexer #(.Bits(32)) multiplexer_9 (
    .sel(and_8_out), .in_0(multiplexer_7_out), .in_1(DispA), .out(multiplexer_9_out));
  Multiplexer #(.Bits(32)) multiplexer_10 (
    .sel(and_10_out), .in_0(multiplexer_9_out), .in_1(DispB), .out(multiplexer_10_out));
  Multiplexer #(.Bits(32)) multiplexer_11 (
    .sel(and_12_out), .in_0(multiplexer_10_out), .in_1({{27{1'b0}}, DispXIndex_q}), .out(multiplexer_11_out));
  Multiplexer #(.Bits(32)) multiplexer_12 (
    .sel(and_14_out), .in_0(multiplexer_11_out), .in_1(DispCValues_q),
    .out({multiplexer_12_out_2, multiplexer_12_out}));
  Seven_Seg_Hex seven_seg_hex_1 (.d(DispA[31:28]), .dp(1'b0));
  Seven_Seg_Hex seven_seg_hex_2 (.d(DispB[31:28]), .dp(1'b0));
  Seven_Seg_Hex seven_seg_hex_3 (.d(DispA[27:24]), .dp(1'b0));
  Seven_Seg_Hex seven_seg_hex_4 (.d(DispB[27:24]), .dp(1'b0));
  Seven_Seg_Hex seven_seg_hex_5 (.d(DispA[23:20]), .dp(1'b0));
  Seven_Seg_Hex seven_seg_hex_6 (.d(DispB[23:20]), .dp(1'b0));
  Seven_Seg_Hex seven_seg_hex_7 (.d(DispA[19:16]), .dp(1'b0));
  Seven_Seg_Hex seven_seg_hex_8 (.d(DispB[19:16]), .dp(1'b0));
  Seven_Seg_Hex seven_seg_hex_9 (.d(DispA[15:12]), .dp(1'b0));
  Seven_Seg_Hex seven_seg_hex_10 (.d(DispB[15:12]), .dp(1'b0));
  Seven_Seg_Hex seven_seg_hex_11 (.d(DispA[11:8]), .dp(1'b0));
  Seven_Seg_Hex seven_seg_hex_12 (.d(DispB[11:8]), .dp(1'b0));
  Seven_Seg_Hex seven_seg_hex_13 (.d(DispA[7:4]), .dp(1'b0));
  Seven_Seg_Hex seven_seg_hex_14 (.d(DispB[7:4]), .dp(1'b0));
  Seven_Seg_Hex seven_seg_hex_15 (.d(DispA[3:0]), .dp(1'b0));
  Seven_Seg_Hex seven_seg_hex_16 (.d(DispB[3:0]), .dp(1'b0));

  // Other names for the same wires on the sheet: MemAddr[13:0] = Addr[13:0]; In_SrcDest = Addr_Step;
  //   In_Temp = Addr_Src; In_Dev = Addr_Dest; Out_Temp = Addr_Dest

  // Notes on the sheet:
  //   clk: Hz: 4
  //   contents of Addr_Match (hex, n*v repeats v):
  //   61440*0,1,2,4,8,e,1a,34,80,ae,14a,214
  //   rom_1 loads program.bin
  //   Load pointers
  //   Read Source
  //   Write Destination
  //   Increment Step
  //   Control changes on -Clk
  //   Data changes on +Clk
  //   0x0000-0x3FFF : ROM
  //   0x4000-0x7FFF : RAM
  //   0xF000-0xF00A : ALU A, B,
  //   SUM, AND, OR, XOR, NOT,
  //   GT, GTE, LT, LTE
  //   0xF100 : Display A
  //   0xF101 : Display B
  //   0xF200 : Matrix X index
  //   0xF201 : Matrix Column values
  //   0xFFFF : Step
endmodule
